# Fritzing sketch ESP-temp-module-v2 (saved by Fritzing 0.9.3b)
circuit board: 8.46667cm x 5.64444cm
breadboards: 1

parts:
  U1 = ESP-12F (ESP8266 WiFi Module) [part_number=ESP8266]
  R1 = Resistor [tolerance=±5% resistance=10k package="0402 [SMD]"]
  R2 = Resistor [tolerance=±5% resistance=10k package="0402 [SMD]"]
  R3 = Resistor [tolerance=±5% resistance=10k package="0402 [SMD]"]
  R4 = Resistor [tolerance=±5% resistance=1k package="0402 [SMD]"]
  DHT21 = Humidity and Temperature Sensor RHT03
  VCC_3xAA_or_AAA_or_1x18650 = 4 x AAA Battery Mount
  U2 = V_REG_LD1117VXX [package=78xxl]
  R5 = Resistor [tolerance=±5% resistance=1M package="0402 [SMD]"]
  R6 = Resistor [tolerance=±5% resistance=100k package="0402 [SMD]"]
  Q1 = TRANSISTOR_NPN [part_number=2N2222 package=to-92-ammo]
  WiFi_Rst = Pushbutton [package="[THT]"]

nets:
  VCC: U1.VCC, R2.Pin_1, R3.Pin_1, DHT21.Vcc, U2.OUT
  GND: U1.GPIO0, U1.GND, U1.GPIO15, R1.Pin_0, R1.Pin_1, R2.Pin_0, U2.GND, R6.Pin_0, Q1.E, WiFi_Rst.Pin_3, WiFi_Rst.Pin_4
  N1: U1.GPIO2, DHT21.Data-signal
  N2: U1.EN, R3.Pin_0
  N3: U1.GPIO4, R4.Pin_0
  N4: U1.ADC0, R5.Pin_0, R6.Pin_1
  N5: U1.GPIO16, U1.RST
  N6: U1.GPIO14, WiFi_Rst.Pin_1, WiFi_Rst.Pin_2
  N7: R4.Pin_1, Q1.B
  N8: DHT21.GND_2, Q1.C
  N9: VCC_3xAA_or_AAA_or_1x18650.-, U2.IN, R5.Pin_1

notes:
  Note: R1 and R3 are included with the ESP plate
  ESP Temp Logger, 2

custom parts:
  ESP-12F (ESP8266 WiFi Module): WiFi Module based on the ESP8266 with onboard PCB antenna and UART communications
